# Fritzing sketch stopwatch-board (saved by Fritzing 0.7.12b)
perfboards: 1

parts:
  LCD1 = LCD screen
  XTAL1 = Crystal [frequency="16 Mhz" package=THT]
  C1 = Ceramic Capacitor [capacitance=100nF package="100 mil [THT, multilayer]"]
  C2 = Electrolytic Capacitor [capacitance=1µF package="100 mil [THT, electrolytic]"]
  U1 = Voltage Regulator - 5V [package="TO220 [THT]"]
  IC1 = IC, DIP package, 14 pins [chip_label=ATTiny84]
  S2 = Pushbutton [package="[THT]"]
  VCC1 = Battery
  VCC2 = Battery
  S3 = Pushbutton [package="[THT]"]
  R1 = Resistor [tolerance=±5% resistance=220 package=THT]
  R2 = Resistor [tolerance=±5% resistance=100 package=THT]
  R3 = Resistor [tolerance=±5% resistance=100 package=THT]

nets:
  GND: LCD1.VSS, LCD1.LED-, C1.0, C2.-, U1.GND, IC1.pin14, VCC2.-, R1.Pin_1, R2.Pin_1, R3.Pin_1
  N1: LCD1.VDD, C1.1, U1.output_voltage, IC1.pin1, S2.Pin_3, S2.Pin_4, S3.Pin_3, S3.Pin_4
  N2: LCD1.V0, R3.Pin_0
  N3: LCD1.RS, IC1.pin13
  N4: LCD1.E, IC1.pin12
  N5: LCD1.DB4, IC1.pin11
  N6: LCD1.DB5, IC1.pin10
  N7: LCD1.DB6, IC1.pin9
  N8: LCD1.DB7, IC1.pin8
  N9: LCD1.LED+, IC1.pin7
  N10: XTAL1.pin_0, IC1.pin2
  N11: XTAL1.pin_1, IC1.pin3
  N12: C2.+, U1.input_voltage, VCC1.+
  N13: IC1.pin5, S2.Pin_1, S2.Pin_2, R1.Pin_0
  N14: IC1.pin6, S3.Pin_1, S3.Pin_2, R2.Pin_0
  N15: VCC1.-, VCC2.+
